# Fritzing sketch Line follower wiring schematic (saved by Fritzing 0.9.6b)
breadboards: 1

parts:
  U1 = L9110 H-bridge module [part_number="L9110 H-bridge"]
  M1 = gear-motor [part_number="MOTOR LEFT"]
  M2 = gear-motor [part_number="MOTOR RIGHT"]
  Part1 = Arduino Uno (Rev3)
  BAT1 = BC9VPC [package=bc9vpc]
  VCC1 = 4 x AAA Battery Mount
  M3 = 5-ir-array-sensor [package=THT]
  HC-SR04_Sensor_1 = HC-SR04 Ultrasonic Distance Sensor

nets:
  N1: U1.B-IA, Part1.D5_PWM
  N2: U1.B-IB, Part1.D4
  N3: U1.GND, VCC1.+
  N4: U1.VCC, VCC1.-
  N5: U1.A-IA, Part1.D3_PWM
  N6: U1.A-IB, Part1.D2
  N7: U1.MOTOR_A-A, M2.pin_2
  N8: U1.MOTOR_A-B, M2.pin_1
  N9: U1.MOTOR_B-A, M1.pin_1
  N10: U1.MOTOR_B-B, M1.pin_2
  N11: Part1.A0, M3.S1
  N12: Part1.A1, M3.S2
  N13: Part1.A2, M3.S3
  N14: Part1.A3, M3.S4
  N15: Part1.A4/SDA, M3.S5
  3V3: Part1.3V3, M3.VCC
  5V: Part1.5V, HC-SR04_Sensor_1.VCC
  GND: Part1.GND, BAT1.V-, HC-SR04_Sensor_1.GND
  N16: Part1.VIN, BAT1.V+

custom parts:
  5-ir-array-sensor: 5 IR array sensor.
